# Fritzing sketch circuit (saved by Fritzing 1.0.1rc)

parts:
  Componente1 = Arduino Nano (Rev3.0)
  J1 = Basic Servo
  J2 = Basic Servo
  Componente2 = InvenSense MPU6050
  BAT1 = BC9VPC [package=bc9vpc]
  U1 = SWITCH-SPST-2 [package=switch-spst-vertical]

nets:
  GND: Componente1.GND, J1.gnd, J2.gnd, Componente2.GND
  N1: Componente1.D7, J1.pulse
  N2: Componente1.D9, J2.pulse
  N3: Componente1.VIN, BAT1.V+
  VCC: Componente1.5V, J1.vcc, J2.vcc
  N4: Componente1.A5, Componente2.SCL
  N5: Componente1.A4, Componente2.SDA
  3V3: Componente1.3V3, Componente2.VCC
  N6: BAT1.V-, U1.O
